// Logisim project coffeeCircuit.circ as structural Verilog: 1 circuit, main circuit main
module main (
  input  Fifty_Pesos,
  input  Twenty_Pesos,
  input  Ten_Pesos,
  input  Coffee_Choice,
  output Ten_Peso_Change,
  output Twenty_Peso_Change,
  output Fifty_Peso_Change,
  output x2_20_Pesos_Change_Multiplier,
  output Coffee_Output
);

  wire and_1_out, and_2_out, and_3_out, and_4_out, and_5_out, and_6_out, and_7_out, and_8_out, and_9_out,
       and_10_out, not_1_out, not_2_out, not_3_out, not_4_out;

  not not_1 (not_1_out, Fifty_Pesos);
  not not_2 (not_2_out, Twenty_Pesos);
  not not_3 (not_3_out, Ten_Pesos);
  not not_4 (not_4_out, Coffee_Choice);
  and and_1 (and_1_out, Ten_Pesos, not_4_out, not_2_out);
  and and_2 (and_2_out, Coffee_Choice, Ten_Pesos, not_1_out);
  and and_3 (and_3_out, Coffee_Choice, not_3_out, Fifty_Pesos);
  and and_4 (and_4_out, Ten_Pesos, not_2_out, Fifty_Pesos);
  and and_5 (and_5_out, not_4_out, not_3_out, Fifty_Pesos);
  and and_6 (and_6_out, Coffee_Choice, Twenty_Pesos);
  and and_7 (and_7_out, not_3_out, Twenty_Pesos);
  and and_8 (and_8_out, Coffee_Choice, Ten_Pesos, Twenty_Pesos, Fifty_Pesos);
  and and_9 (and_9_out, not_4_out, not_3_out, Twenty_Pesos, Fifty_Pesos);
  and and_10 (and_10_out, not_4_out, Ten_Pesos, Twenty_Pesos);
  or or_1 (Ten_Peso_Change, and_1_out, and_2_out, and_3_out);
  or or_2 (Twenty_Peso_Change, and_4_out, and_5_out, and_6_out, and_7_out);
  and and_11 (Fifty_Peso_Change, not_4_out, Ten_Pesos, Twenty_Pesos, Fifty_Pesos);
  or or_3 (x2_20_Pesos_Change_Multiplier, and_8_out, and_9_out);
  or or_4 (Coffee_Output, and_10_out, Fifty_Pesos);
endmodule
